// Logisim project swap.circ as structural Verilog: 1 circuit, main circuit main
module main (
  input  Barramento,
  input  in_2,
  input  in_3,
  input  in_4,
  input  in_5,
  input  in_6,
  input  in_7,
  input  in_8,
  input  in_9,
  input  in_10,
  input  in_11,
  input  in_12,
  input  in_13,
  input  in_14,
  input  in_15,
  input  in_16,
  input  in_17
);

  wire and_1_out, and_2_out, and_3_out, and_4_out, and_5_out, and_6_out, and_7_out, clock_1_out,
       controlled_buffer_1_out, j_k_ff_1_q, j_k_ff_1_qn, j_k_ff_2_q, j_k_ff_3_q, j_k_ff_3_qn, j_k_ff_4_q,
       j_k_ff_5_q, not_1_out, not_2_out;

  assign controlled_buffer_1_out = in_2 ? Barramento : 1'bz;  // Controlled_Buffer controlled_buffer_1
  Clock clock_1 (.out(clock_1_out));
  and and_1 (and_1_out, j_k_ff_3_q, j_k_ff_1_q);
  J_K_Flip_Flop j_k_ff_1 (
    .J(j_k_ff_1_qn), .clk(clock_1_out), .K(not_1_out), .Q(j_k_ff_1_q), .Qn(j_k_ff_1_qn), .preset(in_12),
    .en(in_13), .reset(in_14));
  not not_1 (not_1_out, j_k_ff_1_qn);
  J_K_Flip_Flop j_k_ff_2 (
    .J(controlled_buffer_1_out), .clk(clock_1_out), .K(in_3), .Q(j_k_ff_2_q), .preset(in_4), .en(and_1_out),
    .reset(in_5));  // open: Qn
  and and_2 (and_2_out, j_k_ff_3_q, ~j_k_ff_1_q);  // AND_Gate
  assign controlled_buffer_1_out = and_2_out ? j_k_ff_2_q : 1'bz;  // Controlled_Buffer controlled_buffer_2
  J_K_Flip_Flop j_k_ff_3 (
    .J(j_k_ff_3_qn), .clk(j_k_ff_1_qn), .K(not_2_out), .Q(j_k_ff_3_q), .Qn(j_k_ff_3_qn), .preset(in_15),
    .en(in_16), .reset(in_17));
  not not_2 (not_2_out, j_k_ff_3_qn);
  J_K_Flip_Flop j_k_ff_4 (
    .J(controlled_buffer_1_out), .clk(clock_1_out), .K(in_6), .Q(j_k_ff_4_q), .preset(in_7), .en(and_3_out),
    .reset(in_8));  // open: Qn
  and and_3 (and_3_out, j_k_ff_3_q, ~j_k_ff_1_q);  // AND_Gate
  assign controlled_buffer_1_out = and_4_out ? j_k_ff_4_q : 1'bz;  // Controlled_Buffer controlled_buffer_3
  and and_4 (and_4_out, ~j_k_ff_3_q, j_k_ff_1_q);  // AND_Gate
  J_K_Flip_Flop j_k_ff_5 (
    .J(controlled_buffer_1_out), .clk(clock_1_out), .K(in_9), .Q(j_k_ff_5_q), .preset(in_10), .en(and_5_out),
    .reset(in_11));  // open: Qn
  and and_5 (and_5_out, ~j_k_ff_3_q, j_k_ff_1_q);  // AND_Gate
  assign controlled_buffer_1_out = and_6_out ? j_k_ff_5_q : 1'bz;  // Controlled_Buffer controlled_buffer_4
  and and_6 (and_6_out, j_k_ff_3_q, j_k_ff_1_q);
  LED led_1 (.in(and_7_out));
  and and_7 (and_7_out, ~j_k_ff_1_q, ~j_k_ff_3_q);  // AND_Gate

  // Notes on the sheet:
  //   clk
  //   c1
  //   h1
  //   c2
  //   w2
  //   w1
  //   h2
  //   c3
  //   h3
endmodule
