// Logisim project swap2.circ as structural Verilog: 1 circuit, main circuit main
module main (
  input  Barramento,
  input  in_2,
  input  in_3,
  input  in_4,
  input  in_5,
  input  in_6,
  input  in_7,
  input  in_8,
  input  in_9,
  input  in_10,
  input  in_11,
  input  W,
  input  in_13,
  input  JK2,
  input  in_15,
  input  JK1,
  input  in_17,
  input  in_18
);

  wire and_1_out, and_2_out, and_3_out, and_4_out, and_5_out, and_6_out, and_7_out, and_8_out, and_9_out,
       and_10_out, and_11_out, clock_1_out, controlled_buffer_1_out, j_k_ff_1_q, j_k_ff_2_q, j_k_ff_3_q,
       j_k_ff_4_q, j_k_ff_5_q;

  Clock clock_1 (.out(clock_1_out));
  assign controlled_buffer_1_out = in_2 ? Barramento : 1'bz;  // Controlled_Buffer controlled_buffer_1
  and and_1 (and_1_out, W, ~j_k_ff_4_q, ~j_k_ff_2_q);  // AND_Gate
  and and_2 (and_2_out, ~j_k_ff_4_q, j_k_ff_2_q);  // AND_Gate
  J_K_Flip_Flop j_k_ff_1 (
    .J(controlled_buffer_1_out), .clk(clock_1_out), .K(in_3), .Q(j_k_ff_1_q), .preset(in_4), .en(and_3_out),
    .reset(in_5));  // open: Qn
  and and_3 (and_3_out, j_k_ff_4_q, ~j_k_ff_2_q);  // AND_Gate
  J_K_Flip_Flop j_k_ff_2 (
    .J(and_1_out), .clk(clock_1_out), .K(and_2_out), .Q(j_k_ff_2_q), .preset(in_13), .en(JK2), .reset(in_15));  // open: Qn
  assign controlled_buffer_1_out = and_4_out ? j_k_ff_1_q : 1'bz;  // Controlled_Buffer controlled_buffer_2
  and and_4 (and_4_out, ~j_k_ff_4_q, j_k_ff_2_q);  // AND_Gate
  and and_5 (and_5_out, ~j_k_ff_4_q, j_k_ff_2_q);  // AND_Gate
  and and_6 (and_6_out, j_k_ff_4_q, ~j_k_ff_2_q);  // AND_Gate
  J_K_Flip_Flop j_k_ff_3 (
    .J(controlled_buffer_1_out), .clk(clock_1_out), .K(in_6), .Q(j_k_ff_3_q), .preset(in_7), .en(and_7_out),
    .reset(in_8));  // open: Qn
  and and_7 (and_7_out, ~j_k_ff_4_q, j_k_ff_2_q);  // AND_Gate
  J_K_Flip_Flop j_k_ff_4 (
    .J(and_5_out), .clk(clock_1_out), .K(and_6_out), .Q(j_k_ff_4_q), .preset(JK1), .en(in_17), .reset(in_18));  // open: Qn
  assign controlled_buffer_1_out = and_8_out ? j_k_ff_3_q : 1'bz;  // Controlled_Buffer controlled_buffer_3
  and and_8 (and_8_out, ~j_k_ff_4_q, W, ~j_k_ff_2_q);  // AND_Gate
  J_K_Flip_Flop j_k_ff_5 (
    .J(controlled_buffer_1_out), .clk(clock_1_out), .K(in_9), .Q(j_k_ff_5_q), .preset(in_10),
    .en(and_10_out), .reset(in_11));  // open: Qn
  and and_9 (and_9_out, j_k_ff_4_q, ~j_k_ff_2_q);  // AND_Gate
  and and_10 (and_10_out, ~j_k_ff_4_q, W, ~j_k_ff_2_q);  // AND_Gate
  assign controlled_buffer_1_out = and_9_out ? j_k_ff_5_q : 1'bz;  // Controlled_Buffer controlled_buffer_4
  LED led_1 (.in(and_11_out));
  and and_11 (and_11_out, ~j_k_ff_2_q, ~W, ~j_k_ff_4_q);  // AND_Gate

  // Notes on the sheet:
  //   clk
  //   W
  //   c1
  //   Q2
  //   h1
  //   Q2
  //   Q1
  //   h2
  //   c2
  //   c3
  //   Q1
  //   h3
endmodule
