// Logisim project t4sistemas.circ as structural Verilog: 1 circuit, main circuit main
module main (
  input  \Início ,
  input  Zero,
  input  in_3,
  input  in_4,
  input  in_5,
  input  in_6
);

  wire adder_1_cout, and_1_out, and_2_out, button_1_out, clock_1_out, counter_1_carry, j_k_ff_1_q,
       j_k_ff_1_qn, j_k_ff_2_q, j_k_ff_2_qn, not_1_out, or_1_out, or_2_out, xnor_1_out;
  wire [7:0] adder_1_out, register_1_q;

  Clock clock_1 (.out(clock_1_out));
  not not_1 (not_1_out, counter_1_carry);
  or or_1 (or_1_out, \Início , j_k_ff_1_q);
  or or_2 (or_2_out, j_k_ff_1_q, not_1_out);
  Button button_1 (.out(button_1_out));
  J_K_Flip_Flop j_k_ff_1 (
    .J(j_k_ff_2_q), .clk(clock_1_out), .K(j_k_ff_1_q), .Q(j_k_ff_1_q), .Qn(j_k_ff_1_qn), .preset(in_3),
    .en(in_4), .reset(button_1_out));
  J_K_Flip_Flop j_k_ff_2 (
    .J(or_1_out), .clk(clock_1_out), .K(or_2_out), .Q(j_k_ff_2_q), .Qn(j_k_ff_2_qn), .preset(in_5),
    .en(in_6), .reset(button_1_out));
  and and_1 (and_1_out, j_k_ff_1_qn, j_k_ff_2_qn);
  and and_2 (and_2_out, j_k_ff_1_q, j_k_ff_2_qn);
  xnor xnor_1 (xnor_1_out, j_k_ff_1_q, j_k_ff_2_q);
  LED led_1 (.in(xnor_1_out));
  Register register_1 (.D(adder_1_out), .Q(register_1_q), .clk(and_2_out), .clr(and_1_out));  // open: en
  LED led_2 (.in(adder_1_cout));
  Counter #(.width(3), .max('h4)) counter_1 (
    .load(1'b0), .count(1'b1), .carry(counter_1_carry), .clk(and_2_out), .clr(and_1_out));  // open: D, Q
  Adder adder_1 (.a(register_1_q), .b(8'h70), .out(adder_1_out), .cout(adder_1_cout));  // open: cin
  // Probe on register_1_q
  Adder adder_2 ();  // open: a, b, out, cin, cout

  // Notes on the sheet:
  //   Clock
  //   zero
  //   Reset
  //   JK1
  //   JK0
  //   set/rec
  //   dec/cac
  //   Pronto
  //   acum
  //   entrada
  //   count
  //   somador
  //   overflow
  //   somador
endmodule
